// Logisim project 实验1.circ as structural Verilog: 5 circuits, main circuit 一位二进制半加器
module \一位二进制半加器  (
  input  A,
  input  B,
  output S,
  output C
);

  xor xor_1 (S, A, B);
  and and_1 (C, A, B);
endmodule

module \一位二进制全加器  (
  input  A,
  input  B,
  input  Ci,
  output S,
  output Co
);

  wire nand_1_out, nand_2_out, xor_1_out;

  xor xor_1 (xor_1_out, A, B);
  nand nand_1 (nand_1_out, xor_1_out, Ci);
  nand nand_2 (nand_2_out, B, A);
  xor xor_2 (S, xor_1_out, Ci);
  nand nand_3 (Co, nand_1_out, nand_2_out);
endmodule

module \串行进位并行加法器  (
  input  C0,
  input  A3,
  input  B3,
  input  A2,
  input  B2,
  input  A1,
  input  B1,
  input  A0,
  input  B0,
  output S3,
  output S2,
  output S1,
  output S0,
  output C4
);

  wire \一位二进制全加器_2_co , \一位二进制全加器_3_co , \一位二进制全加器_4_co ;

  \一位二进制全加器  \u_一位二进制全加器_1  (.A(A3), .B(B3), .Ci(\一位二进制全加器_2_co ), .S(S3), .Co(C4));
  \一位二进制全加器  \u_一位二进制全加器_2  (.A(A2), .B(B2), .Ci(\一位二进制全加器_3_co ), .S(S2), .Co(\一位二进制全加器_2_co ));
  \一位二进制全加器  \u_一位二进制全加器_3  (.A(A1), .B(B1), .Ci(\一位二进制全加器_4_co ), .S(S1), .Co(\一位二进制全加器_3_co ));
  \一位二进制全加器  \u_一位二进制全加器_4  (.A(A0), .B(B0), .Ci(C0), .S(S0), .Co(\一位二进制全加器_4_co ));

  // Notes on the sheet:
  //   C3
  //   C2
  //   C1
endmodule

module \先行进位并行加法器  (
  input  C0,
  input  A0,
  input  B0,
  input  A1,
  input  B1,
  input  A2,
  input  B2,
  input  A3,
  input  B3,
  output S0,
  output S1,
  output S2,
  output S3,
  output C4
);

  wire and_1_out, and_2_out, and_3_out, and_4_out, and_5_out, and_6_out, and_7_out, and_8_out, and_9_out,
       and_10_out, C1_out, C2_out, C3_out, G0_out, G1_out, G2_out, G3_out, P0_out, P1_out, P2_out, P3_out;

  xor P0 (P0_out, A0, B0);
  xor P1 (P1_out, A1, B1);
  xor P2 (P2_out, A2, B2);
  xor P3 (P3_out, A3, B3);
  and G0 (G0_out, A0, B0);
  and G1 (G1_out, A1, B1);
  and G2 (G2_out, A2, B2);
  and G3 (G3_out, A3, B3);
  and and_1 (and_1_out, C0, P0_out);
  and and_2 (and_2_out, P0_out, C0, P1_out);
  and and_3 (and_3_out, G0_out, P1_out);
  and and_4 (and_4_out, P1_out, P0_out, C0, P2_out);
  and and_5 (and_5_out, P2_out, P1_out, G0_out);
  and and_6 (and_6_out, P2_out, G1_out);
  and and_7 (and_7_out, P3_out, P2_out, P1_out, P0_out, C0);
  and and_8 (and_8_out, P3_out, P2_out, P1_out, G0_out);
  and and_9 (and_9_out, P3_out, P2_out, G1_out);
  and and_10 (and_10_out, P3_out, G2_out);
  or C1 (C1_out, G0_out, and_1_out);
  or C2 (C2_out, and_2_out, and_3_out, G1_out);
  or C3 (C3_out, and_4_out, and_5_out, and_6_out, G2_out);
  or u_C4 (C4, and_7_out, and_8_out, and_9_out, and_10_out, G3_out);
  xor xor_1 (S0, C0, P0_out);
  xor xor_2 (S1, C1_out, P1_out);
  xor xor_3 (S2, C2_out, P2_out);
  xor xor_4 (S3, C3_out, P3_out);
endmodule

module \先行进位并行加法器测试电路  (
  input  C0,
  input  A,
  input  in_3,
  input  in_4,
  input  in_5,
  input  B,
  input  in_7,
  input  in_8,
  input  in_9,
  output S,
  output out_11,
  output out_12,
  output out_13,
  output C4
);

  \先行进位并行加法器  \u_先行进位并行加法器_1  (
    .C0(C0), .A0(in_5), .B0(in_9), .A1(in_4), .B1(in_8), .A2(in_3), .B2(in_7), .A3(A), .B3(B), .S0(out_13),
    .S1(out_12), .S2(out_11), .S3(S), .C4(C4));
endmodule
