// Logisim project 实验2.circ as structural Verilog: 10 circuits, main circuit 先行进位并行加法器
module \先行进位并行加法器  (
  input  C0,
  input  A0,
  input  B0,
  input  A1,
  input  B1,
  input  A2,
  input  B2,
  input  A3,
  input  B3,
  output S0,
  output S1,
  output S2,
  output S3,
  output C4
);

  wire and_1_out, and_2_out, and_3_out, and_4_out, and_5_out, and_6_out, and_7_out, and_8_out, and_9_out,
       and_10_out, C1_out, C2_out, C3_out, G0_out, G1_out, G2_out, G3_out, P0_out, P1_out, P2_out, P3_out;

  xor P0 (P0_out, A0, B0);
  xor P1 (P1_out, A1, B1);
  xor P2 (P2_out, A2, B2);
  xor P3 (P3_out, A3, B3);
  and G0 (G0_out, A0, B0);
  and G1 (G1_out, A1, B1);
  and G2 (G2_out, A2, B2);
  and G3 (G3_out, A3, B3);
  and and_1 (and_1_out, C0, P0_out);
  and and_2 (and_2_out, P0_out, C0, P1_out);
  and and_3 (and_3_out, G0_out, P1_out);
  and and_4 (and_4_out, P1_out, P0_out, C0, P2_out);
  and and_5 (and_5_out, P2_out, P1_out, G0_out);
  and and_6 (and_6_out, P2_out, G1_out);
  and and_7 (and_7_out, P3_out, P2_out, P1_out, P0_out, C0);
  and and_8 (and_8_out, P3_out, P2_out, P1_out, G0_out);
  and and_9 (and_9_out, P3_out, P2_out, G1_out);
  and and_10 (and_10_out, P3_out, G2_out);
  or C1 (C1_out, G0_out, and_1_out);
  or C2 (C2_out, and_2_out, and_3_out, G1_out);
  or C3 (C3_out, and_4_out, and_5_out, and_6_out, G2_out);
  or u_C4 (C4, and_7_out, and_8_out, and_9_out, and_10_out, G3_out);
  xor xor_1 (S0, C0, P0_out);
  xor xor_2 (S1, C1_out, P1_out);
  xor xor_3 (S2, C2_out, P2_out);
  xor xor_4 (S3, C3_out, P3_out);
endmodule

module \四位二进制可逆计数器  (
  input  CLR,
  input  nLD,
  input  A,
  input  CPD,
  input  CPU,
  input  B,
  input  C,
  input  D,
  output QA,
  output QB,
  output QC,
  output QD
);

  wire and_1_out, and_2_out, and_3_out, and_4_out, and_5_out, and_6_out, and_7_out, and_8_out, and_9_out,
       and_10_out, and_11_out, and_12_out, and_13_out, and_14_out, D1_qn, D2_qn, D3_qn, D4_qn, not_1_out,
       not_2_out, not_3_out, not_4_out, not_5_out, not_6_out, not_7_out, not_8_out, or_1_out, or_2_out,
       or_3_out, or_4_out, or_5_out, or_6_out, or_7_out, or_8_out;

  not not_1 (not_1_out, QA);
  not not_2 (not_2_out, QB);
  not not_3 (not_3_out, QC);
  and and_1 (and_1_out, CPU, QA);
  and and_2 (and_2_out, CPD, not_1_out);
  and and_3 (and_3_out, QA, CPU, QB);
  and and_4 (and_4_out, not_1_out, not_2_out, CPD);
  and and_5 (and_5_out, QB, QA, CPU, QC);
  and and_6 (and_6_out, not_2_out, not_1_out, not_3_out, CPD);
  or or_1 (or_1_out, CPD, CPU);
  or or_2 (or_2_out, and_1_out, and_2_out);
  or or_3 (or_3_out, and_3_out, and_4_out);
  or or_4 (or_4_out, and_5_out, and_6_out);
  D_Flip_Flop #(.trigger("falling"), .Pre_Clr_Positions("BELOW_ABOVE"), .NegatePresetClear("false"), .enable("false"), .NewFFLayout("true")) D1 (
    .clk(or_1_out), .D(D1_qn), .Q(QA), .Qn(D1_qn), .preset(and_8_out), .reset(or_5_out));
  D_Flip_Flop #(.trigger("falling"), .Pre_Clr_Positions("BELOW_ABOVE"), .NegatePresetClear("false"), .enable("false"), .NewFFLayout("true")) D2 (
    .clk(or_2_out), .D(D2_qn), .Q(QB), .Qn(D2_qn), .preset(and_10_out), .reset(or_6_out));
  D_Flip_Flop #(.trigger("falling"), .Pre_Clr_Positions("BELOW_ABOVE"), .NegatePresetClear("false"), .enable("false"), .NewFFLayout("true")) D3 (
    .clk(or_3_out), .D(D3_qn), .Q(QC), .Qn(D3_qn), .preset(and_12_out), .reset(or_7_out));
  D_Flip_Flop #(.trigger("falling"), .Pre_Clr_Positions("BELOW_ABOVE"), .NegatePresetClear("false"), .enable("false"), .NewFFLayout("true")) D4 (
    .clk(or_4_out), .D(D4_qn), .Q(QD), .Qn(D4_qn), .preset(and_14_out), .reset(or_8_out));
  or or_5 (or_5_out, CLR, and_7_out);
  or or_6 (or_6_out, CLR, and_9_out);
  or or_7 (or_7_out, CLR, and_11_out);
  or or_8 (or_8_out, CLR, and_13_out);
  and and_7 (and_7_out, not_5_out, not_4_out);
  and and_8 (and_8_out, not_4_out, A);
  and and_9 (and_9_out, not_6_out, not_4_out);
  and and_10 (and_10_out, not_4_out, B);
  and and_11 (and_11_out, not_7_out, not_4_out);
  and and_12 (and_12_out, not_4_out, C);
  and and_13 (and_13_out, not_8_out, not_4_out);
  and and_14 (and_14_out, not_4_out, D);
  not not_4 (not_4_out, nLD);
  not not_5 (not_5_out, A);
  not not_6 (not_6_out, B);
  not not_7 (not_7_out, C);
  not not_8 (not_8_out, D);
endmodule

module \四位二进制可逆计数器测试电路  (
  input  in_1,
  input  in_2,
  input  in_3,
  input  in_4,
  input  in_5,
  input  in_6,
  input  in_7,
  input  in_8,
  output out_9,
  output out_10,
  output out_11,
  output out_12
);

  \四位二进制可逆计数器  \u_四位二进制可逆计数器_1  (
    .CPD(in_3), .CPU(in_1), .CLR(in_2), .nLD(in_8), .A(in_7), .QA(out_12), .B(in_6), .QB(out_11), .C(in_5),
    .QC(out_10), .D(in_4), .QD(out_9));
endmodule

module \二进制转8421码电路  (
  input  A3,
  input  A2,
  input  A1,
  input  A0,
  output S13,
  output S12,
  output S11,
  output S10,
  output S3,
  output S2,
  output S1,
  output S0
);

  wire and_1_out, and_2_out, or_1_out;

  and and_1 (and_1_out, A3, A2);
  \先行进位并行加法器  \u_先行进位并行加法器_1  (
    .C0(1'b0), .A0(A0), .B0(1'b0), .A1(A1), .B1(or_1_out), .A2(A2), .B2(or_1_out), .A3(A3), .B3(1'b0),
    .S0(S0), .S1(S1), .S2(S2), .S3(S3), .C4(S10));
  or or_1 (or_1_out, and_1_out, and_2_out);
  and and_2 (and_2_out, A1, A3);

  assign S11 = 1'b0;
  assign S12 = 1'b0;
  assign S13 = 1'b0;
endmodule

module \二进制转8421码测试电路  (
  input  \二进制 ,
  input  in_2,
  input  in_3,
  input  in_4,
  output \_8421码 ,
  output out_6,
  output out_7,
  output out_8,
  output out_9,
  output out_10,
  output out_11,
  output out_12
);

  \二进制转8421码电路  \u_二进制转8421码电路_1  (
    .A3(\二进制 ), .A2(in_2), .A1(in_3), .A0(in_4), .S13(\_8421码 ), .S12(out_6), .S11(out_7), .S10(out_8),
    .S3(out_9), .S2(out_10), .S1(out_11), .S0(out_12));
endmodule

module \显示电路  (
  input  A3,
  input  A2,
  input  A1,
  input  A0,
  output a,
  output b,
  output c,
  output d,
  output e,
  output f,
  output g
);

  wire and_1_out, and_2_out, and_3_out, and_4_out, and_5_out, and_6_out, and_7_out, and_8_out, and_9_out,
       and_10_out, and_11_out, and_12_out, and_13_out, and_14_out, and_15_out, and_16_out, and_17_out,
       and_18_out, and_19_out, and_20_out, and_21_out, and_22_out, and_23_out, and_24_out, and_25_out,
       not_1_out, not_2_out, not_3_out, not_4_out;

  not not_1 (not_1_out, A3);
  not not_2 (not_2_out, A2);
  not not_3 (not_3_out, A1);
  not not_4 (not_4_out, A0);
  and and_1 (and_1_out, not_1_out, not_2_out, not_4_out);
  and and_2 (and_2_out, not_2_out, not_1_out, A1);
  and and_3 (and_3_out, not_1_out, A2, A0);
  and and_4 (and_4_out, not_2_out, not_3_out, A3);
  and and_5 (and_5_out, not_1_out, not_2_out);
  and and_6 (and_6_out, not_1_out, not_3_out, not_4_out);
  and and_7 (and_7_out, not_1_out, A1, A0);
  and and_8 (and_8_out, not_2_out, not_3_out);
  and and_9 (and_9_out, not_2_out, not_3_out);
  and and_10 (and_10_out, not_1_out, A0);
  and and_11 (and_11_out, not_1_out, A2);
  and and_12 (and_12_out, not_2_out, not_3_out, not_4_out);
  and and_13 (and_13_out, not_1_out, not_2_out, A1);
  and and_14 (and_14_out, not_1_out, not_3_out, A2, A0);
  and and_15 (and_15_out, not_1_out, not_4_out, A1);
  and and_16 (and_16_out, not_2_out, not_3_out, not_4_out);
  and and_17 (and_17_out, not_1_out, not_4_out, A1);
  and and_18 (and_18_out, not_1_out, not_3_out, not_4_out);
  and and_19 (and_19_out, not_1_out, not_3_out, A2);
  and and_20 (and_20_out, not_1_out, not_4_out, A2);
  and and_21 (and_21_out, not_2_out, not_3_out, A3);
  and and_22 (and_22_out, not_1_out, not_2_out, A1);
  and and_23 (and_23_out, not_1_out, not_3_out, A2);
  and and_24 (and_24_out, not_1_out, not_4_out, A2);
  and and_25 (and_25_out, not_2_out, not_3_out, A3);
  or or_1 (a, and_1_out, and_2_out, and_3_out, and_4_out);
  or or_2 (b, and_5_out, and_6_out, and_7_out, and_8_out);
  or or_3 (c, and_9_out, and_10_out, and_11_out);
  or or_4 (d, and_12_out, and_13_out, and_14_out, and_15_out);
  or or_5 (e, and_16_out, and_17_out);
  or or_6 (f, and_18_out, and_19_out, and_20_out, and_21_out);
  or or_7 (g, and_22_out, and_23_out, and_24_out, and_25_out);
endmodule

module \显示电路测试电路  (
  input  in_1,
  input  in_2,
  input  in_3,
  input  in_4
);

  wire \二进制转8421码电路_1_s0 , \二进制转8421码电路_1_s1 , \二进制转8421码电路_1_s2 , \二进制转8421码电路_1_s3 , \二进制转8421码电路_1_s10 ,
       \二进制转8421码电路_1_s11 , \二进制转8421码电路_1_s12 , \二进制转8421码电路_1_s13 , \显示电路_1_a , \显示电路_1_b , \显示电路_1_c ,
       \显示电路_1_d , \显示电路_1_e , \显示电路_1_f , \显示电路_1_g , \显示电路_2_a , \显示电路_2_b , \显示电路_2_c , \显示电路_2_d ,
       \显示电路_2_e , \显示电路_2_f , \显示电路_2_g ;

  _7_Segment_Display #(.active("true")) u_7_segment_display_1 (
    .g(\显示电路_1_g ), .f(\显示电路_1_f ), .a(\显示电路_1_a ), .b(\显示电路_1_b ), .e(\显示电路_1_e ), .d(\显示电路_1_d ),
    .c(\显示电路_1_c ), .dp(1'b0));
  \显示电路  \u_显示电路_1  (
    .A3(\二进制转8421码电路_1_s13 ), .A2(\二进制转8421码电路_1_s12 ), .A1(\二进制转8421码电路_1_s11 ), .A0(\二进制转8421码电路_1_s10 ),
    .a(\显示电路_1_a ), .b(\显示电路_1_b ), .c(\显示电路_1_c ), .d(\显示电路_1_d ), .e(\显示电路_1_e ), .f(\显示电路_1_f ),
    .g(\显示电路_1_g ));
  \二进制转8421码电路  \u_二进制转8421码电路_1  (
    .A3(in_1), .A2(in_2), .A1(in_3), .A0(in_4), .S13(\二进制转8421码电路_1_s13 ), .S12(\二进制转8421码电路_1_s12 ),
    .S11(\二进制转8421码电路_1_s11 ), .S10(\二进制转8421码电路_1_s10 ), .S3(\二进制转8421码电路_1_s3 ), .S2(\二进制转8421码电路_1_s2 ),
    .S1(\二进制转8421码电路_1_s1 ), .S0(\二进制转8421码电路_1_s0 ));
  _7_Segment_Display #(.active("true")) u_7_segment_display_2 (
    .g(\显示电路_2_g ), .f(\显示电路_2_f ), .a(\显示电路_2_a ), .b(\显示电路_2_b ), .e(\显示电路_2_e ), .d(\显示电路_2_d ),
    .c(\显示电路_2_c ), .dp(1'b0));
  \显示电路  \u_显示电路_2  (
    .A3(\二进制转8421码电路_1_s3 ), .A2(\二进制转8421码电路_1_s2 ), .A1(\二进制转8421码电路_1_s1 ), .A0(\二进制转8421码电路_1_s0 ),
    .a(\显示电路_2_a ), .b(\显示电路_2_b ), .c(\显示电路_2_c ), .d(\显示电路_2_d ), .e(\显示电路_2_e ), .f(\显示电路_2_f ),
    .g(\显示电路_2_g ));
endmodule

module \报警电路  (
  input  CPU,
  input  CLR,
  input  CPD,
  input  D,
  input  C,
  input  B,
  input  A,
  input  nLD
);

  wire and_1_out, and_2_out, and_3_out, and_4_out, not_1_out, or_1_out, \四位二进制可逆计数器_1_qa , \四位二进制可逆计数器_1_qb ,
       \四位二进制可逆计数器_1_qc , \四位二进制可逆计数器_1_qd ;

  not not_1 (not_1_out, and_3_out);
  and and_1 (and_1_out, not_1_out, CPU);
  and and_2 (and_2_out, or_1_out, CPD);
  or or_1 (or_1_out, \四位二进制可逆计数器_1_qa , \四位二进制可逆计数器_1_qb , \四位二进制可逆计数器_1_qc , \四位二进制可逆计数器_1_qd );
  and and_3 (and_3_out, \四位二进制可逆计数器_1_qa , \四位二进制可逆计数器_1_qb , \四位二进制可逆计数器_1_qc , \四位二进制可逆计数器_1_qd );
  \四位二进制可逆计数器  \u_四位二进制可逆计数器_1  (
    .CPD(and_2_out), .CPU(and_1_out), .CLR(CLR), .nLD(nLD), .A(A), .QA(\四位二进制可逆计数器_1_qa ), .B(B),
    .QB(\四位二进制可逆计数器_1_qb ), .C(C), .QC(\四位二进制可逆计数器_1_qc ), .D(D), .QD(\四位二进制可逆计数器_1_qd ));
  and and_4 (and_4_out, CPU, and_3_out);
  // Buzzer #(.freq_measure("Hz"), .vol_width(7)) 警报: pin names not known; wires that end beside it: and_4_out
endmodule

module \小型实验室门禁系统  (
  input  CPU,
  input  CLR,
  input  CPD,
  output a10,
  output b10,
  output c10,
  output d10,
  output e10,
  output f10,
  output g10,
  output a1,
  output b1,
  output c1,
  output d1,
  output e1,
  output f1,
  output g1,
  output \警报 
);

  wire and_1_out, and_2_out, and_3_out, not_1_out, or_1_out, \二进制转8421码电路_1_s0 , \二进制转8421码电路_1_s1 ,
       \二进制转8421码电路_1_s2 , \二进制转8421码电路_1_s3 , \二进制转8421码电路_1_s10 , \二进制转8421码电路_1_s11 , \二进制转8421码电路_1_s12 ,
       \二进制转8421码电路_1_s13 , \四位二进制可逆计数器_1_qa , \四位二进制可逆计数器_1_qb , \四位二进制可逆计数器_1_qc , \四位二进制可逆计数器_1_qd ;

  \显示电路  \u_显示电路_1  (
    .A3(\二进制转8421码电路_1_s13 ), .A2(\二进制转8421码电路_1_s12 ), .A1(\二进制转8421码电路_1_s11 ), .A0(\二进制转8421码电路_1_s10 ),
    .a(a10), .b(b10), .c(c10), .d(d10), .e(e10), .f(f10), .g(g10));
  \二进制转8421码电路  \u_二进制转8421码电路_1  (
    .A3(\四位二进制可逆计数器_1_qd ), .A2(\四位二进制可逆计数器_1_qc ), .A1(\四位二进制可逆计数器_1_qb ), .A0(\四位二进制可逆计数器_1_qa ),
    .S13(\二进制转8421码电路_1_s13 ), .S12(\二进制转8421码电路_1_s12 ), .S11(\二进制转8421码电路_1_s11 ),
    .S10(\二进制转8421码电路_1_s10 ), .S3(\二进制转8421码电路_1_s3 ), .S2(\二进制转8421码电路_1_s2 ), .S1(\二进制转8421码电路_1_s1 ),
    .S0(\二进制转8421码电路_1_s0 ));
  \显示电路  \u_显示电路_2  (
    .A3(\二进制转8421码电路_1_s3 ), .A2(\二进制转8421码电路_1_s2 ), .A1(\二进制转8421码电路_1_s1 ), .A0(\二进制转8421码电路_1_s0 ),
    .a(a1), .b(b1), .c(c1), .d(d1), .e(e1), .f(f1), .g(g1));
  not not_1 (not_1_out, and_3_out);
  and and_1 (and_1_out, not_1_out, CPU);
  and and_2 (and_2_out, or_1_out, CPD);
  or or_1 (or_1_out, \四位二进制可逆计数器_1_qa , \四位二进制可逆计数器_1_qb , \四位二进制可逆计数器_1_qc , \四位二进制可逆计数器_1_qd );
  and and_3 (and_3_out, \四位二进制可逆计数器_1_qa , \四位二进制可逆计数器_1_qb , \四位二进制可逆计数器_1_qc , \四位二进制可逆计数器_1_qd );
  \四位二进制可逆计数器  \u_四位二进制可逆计数器_1  (
    .CPD(and_2_out), .CPU(and_1_out), .CLR(CLR), .nLD(1'b1), .A(1'b0), .QA(\四位二进制可逆计数器_1_qa ), .B(1'b0),
    .QB(\四位二进制可逆计数器_1_qb ), .C(1'b0), .QC(\四位二进制可逆计数器_1_qc ), .D(1'b0), .QD(\四位二进制可逆计数器_1_qd ));
  and and_4 (\警报 , CPU, and_3_out);
endmodule

module \小型门禁系统测试电路  (
  input  CPU,
  input  CLR,
  input  CPD
);

  wire \小型实验室门禁系统_1_a1 , \小型实验室门禁系统_1_a10 , \小型实验室门禁系统_1_b1 , \小型实验室门禁系统_1_b10 , \小型实验室门禁系统_1_c1 ,
       \小型实验室门禁系统_1_c10 , \小型实验室门禁系统_1_d1 , \小型实验室门禁系统_1_d10 , \小型实验室门禁系统_1_e1 , \小型实验室门禁系统_1_e10 ,
       \小型实验室门禁系统_1_f1 , \小型实验室门禁系统_1_f10 , \小型实验室门禁系统_1_g1 , \小型实验室门禁系统_1_g10 , \小型实验室门禁系统_1_警报 ;

  _7_Segment_Display #(.active("true")) u_7_segment_display_1 (
    .g(\小型实验室门禁系统_1_g10 ), .f(\小型实验室门禁系统_1_f10 ), .a(\小型实验室门禁系统_1_a10 ), .b(\小型实验室门禁系统_1_b10 ),
    .e(\小型实验室门禁系统_1_e10 ), .d(\小型实验室门禁系统_1_d10 ), .c(\小型实验室门禁系统_1_c10 ), .dp(1'b0));
  _7_Segment_Display #(.active("true")) u_7_segment_display_2 (
    .g(\小型实验室门禁系统_1_g1 ), .f(\小型实验室门禁系统_1_f1 ), .a(\小型实验室门禁系统_1_a1 ), .b(\小型实验室门禁系统_1_b1 ),
    .e(\小型实验室门禁系统_1_e1 ), .d(\小型实验室门禁系统_1_d1 ), .c(\小型实验室门禁系统_1_c1 ), .dp(1'b0));
  \小型实验室门禁系统  \u_小型实验室门禁系统_1  (
    .CPU(CPU), .CLR(CLR), .CPD(CPD), .\警报 (\小型实验室门禁系统_1_警报 ), .a10(\小型实验室门禁系统_1_a10 ),
    .b10(\小型实验室门禁系统_1_b10 ), .c10(\小型实验室门禁系统_1_c10 ), .d10(\小型实验室门禁系统_1_d10 ), .e10(\小型实验室门禁系统_1_e10 ),
    .f10(\小型实验室门禁系统_1_f10 ), .g10(\小型实验室门禁系统_1_g10 ), .a1(\小型实验室门禁系统_1_a1 ), .b1(\小型实验室门禁系统_1_b1 ),
    .c1(\小型实验室门禁系统_1_c1 ), .d1(\小型实验室门禁系统_1_d1 ), .e1(\小型实验室门禁系统_1_e1 ), .f1(\小型实验室门禁系统_1_f1 ),
    .g1(\小型实验室门禁系统_1_g1 ));
  // Buzzer #(.freq_measure("Hz"), .vol_width(7)) buzzer_1: pin names not known; wires that end beside it: \小型实验室门禁系统_1_警报 
endmodule
