// Logisim project 实验3.circ as structural Verilog: 6 circuits, main circuit 四位乘法器
module \四位乘法器  (
  input  [3:0] a,
  input  [3:0] b,
  output [7:0] P
);

  wire [7:0] adder_1_out, adder_2_out, adder_3_out, adder_4_out, bit_extender_1_out, multiplexer_1_out,
       multiplexer_2_out, multiplexer_3_out, shifter_1_out, shifter_2_out, shifter_3_out;

  assign bit_extender_1_out = {{4{1'b0}}, b};  // Bit_Extender bit_extender_1
  Multiplexer #(.select(1), .width(8), .disabled("Z"), .enable("false")) multiplexer_1 (
    .in0({8{1'b0}}), .in1(adder_1_out), .out(multiplexer_1_out), .sel(a[0]));
  Adder #(.width(8)) adder_1 (.a({8{1'b0}}), .b(bit_extender_1_out), .out(adder_1_out));  // open: cin, cout
  Shifter #(.width(8), .shift("ll")) shifter_1 (.in(bit_extender_1_out), .\dist (3'b001), .out(shifter_1_out));
  Adder #(.width(8)) adder_2 (.a(multiplexer_1_out), .b(shifter_1_out), .out(adder_2_out));  // open: cin, cout
  Multiplexer #(.select(1), .width(8), .disabled("Z"), .enable("false")) multiplexer_2 (
    .in0(multiplexer_1_out), .in1(adder_2_out), .out(multiplexer_2_out), .sel(a[1]));
  Shifter #(.width(8), .shift("ll")) shifter_2 (.in(shifter_1_out), .\dist (3'b001), .out(shifter_2_out));
  Adder #(.width(8)) adder_3 (.a(multiplexer_2_out), .b(shifter_2_out), .out(adder_3_out));  // open: cin, cout
  Multiplexer #(.select(1), .width(8), .disabled("Z"), .enable("false")) multiplexer_3 (
    .in0(multiplexer_2_out), .in1(adder_3_out), .out(multiplexer_3_out), .sel(a[2]));
  Shifter #(.width(8), .shift("ll")) shifter_3 (.in(shifter_2_out), .\dist (3'b001), .out(shifter_3_out));
  Multiplexer #(.select(1), .width(8), .disabled("Z"), .enable("false")) multiplexer_4 (
    .in0(multiplexer_3_out), .in1(adder_4_out), .out(P), .sel(a[3]));
  Adder #(.width(8)) adder_4 (.a(multiplexer_3_out), .b(shifter_3_out), .out(adder_4_out));  // open: cin, cout
endmodule

module \四位乘法器测试电路  (
  input  [3:0] a_3_0,
  input  [3:0] b_3_0,
  output [7:0] p_7_0
);

  \四位乘法器  \u_四位乘法器_1  (.a(a_3_0), .b(b_3_0), .P(p_7_0));
endmodule

module \_32X4乘法器  (
  input  [3:0] a,
  input  [31:0] b,
  output [31:0] P
);

  wire [31:0] adder_1_out, adder_2_out, adder_3_out, adder_4_out, multiplexer_1_out, multiplexer_2_out,
       multiplexer_3_out, shifter_1_out, shifter_2_out, shifter_3_out;

  Multiplexer #(.select(1), .width(32), .disabled("Z"), .enable("false")) multiplexer_1 (
    .in0({32{1'b0}}), .in1(adder_1_out), .out(multiplexer_1_out), .sel(a[0]));
  Adder #(.width(32)) adder_1 (.a({32{1'b0}}), .b(b), .out(adder_1_out));  // open: cin, cout
  Shifter #(.width(32), .shift("ll")) shifter_1 (.in(b), .\dist (5'b00001), .out(shifter_1_out));
  Adder #(.width(32)) adder_2 (.a(multiplexer_1_out), .b(shifter_1_out), .out(adder_2_out));  // open: cin, cout
  Multiplexer #(.select(1), .width(32), .disabled("Z"), .enable("false")) multiplexer_2 (
    .in0(multiplexer_1_out), .in1(adder_2_out), .out(multiplexer_2_out), .sel(a[1]));
  Shifter #(.width(32), .shift("ll")) shifter_2 (.in(shifter_1_out), .\dist (5'b00001), .out(shifter_2_out));
  Adder #(.width(32)) adder_3 (.a(multiplexer_2_out), .b(shifter_2_out), .out(adder_3_out));  // open: cin, cout
  Multiplexer #(.select(1), .width(32), .disabled("Z"), .enable("false")) multiplexer_3 (
    .in0(multiplexer_2_out), .in1(adder_3_out), .out(multiplexer_3_out), .sel(a[2]));
  Shifter #(.width(32), .shift("ll")) shifter_3 (.in(shifter_2_out), .\dist (5'b00001), .out(shifter_3_out));
  Multiplexer #(.select(1), .width(32), .disabled("Z"), .enable("false")) multiplexer_4 (
    .in0(multiplexer_3_out), .in1(adder_4_out), .out(P), .sel(a[3]));
  Adder #(.width(32)) adder_4 (.a(multiplexer_3_out), .b(shifter_3_out), .out(adder_4_out));  // open: cin, cout
endmodule

module \_32X4乘法器测试电路  (
  input  [3:0] a,
  input  [31:0] b,
  output [31:0] p
);

  \_32X4乘法器  \u_32x4乘法器_1  (.a(a), .b(b), .P(p));
endmodule

module \_32X32乘法器  (
  input  [31:0] a,
  input  [31:0] b,
  output [31:0] p
);

  wire [31:0] adder_1_out, adder_2_out, adder_3_out, adder_4_out, adder_5_out, adder_6_out, \n32x4乘法器_1_p ,
       \n32x4乘法器_2_p , \n32x4乘法器_3_p , \n32x4乘法器_4_p , \n32x4乘法器_5_p , \n32x4乘法器_6_p , \n32x4乘法器_7_p ,
       \n32x4乘法器_8_p ;

  \_32X4乘法器  \u_32x4乘法器_1  (.a(a[15:12]), .b(b), .P(\n32x4乘法器_1_p ));
  \_32X4乘法器  \u_32x4乘法器_2  (.a(a[31:28]), .b(b), .P(\n32x4乘法器_2_p ));
  \_32X4乘法器  \u_32x4乘法器_3  (.a(a[11:8]), .b(b), .P(\n32x4乘法器_3_p ));
  \_32X4乘法器  \u_32x4乘法器_4  (.a(a[27:24]), .b(b), .P(\n32x4乘法器_4_p ));
  \_32X4乘法器  \u_32x4乘法器_5  (.a(a[7:4]), .b(b), .P(\n32x4乘法器_5_p ));
  \_32X4乘法器  \u_32x4乘法器_6  (.a(a[23:20]), .b(b), .P(\n32x4乘法器_6_p ));
  \_32X4乘法器  \u_32x4乘法器_7  (.a(a[3:0]), .b(b), .P(\n32x4乘法器_7_p ));
  \_32X4乘法器  \u_32x4乘法器_8  (.a(a[19:16]), .b(b), .P(\n32x4乘法器_8_p ));
  Adder #(.width(32)) adder_1 (
    .a(\n32x4乘法器_7_p ), .b({\n32x4乘法器_5_p [27:0], 4'b0000}), .out(adder_1_out));  // open: cin, cout
  Adder #(.width(32)) adder_2 (
    .a({\n32x4乘法器_3_p [23:0], {8{1'b0}}}), .b({\n32x4乘法器_1_p [19:0], {12{1'b0}}}), .out(adder_2_out));  // open: cin, cout
  Adder #(.width(32)) adder_3 (.a(adder_1_out), .b(adder_2_out), .out(adder_3_out));  // open: cin, cout
  Adder #(.width(32)) adder_4 (
    .a({\n32x4乘法器_8_p [15:0], {16{1'b0}}}), .b({\n32x4乘法器_6_p [11:0], {20{1'b0}}}), .out(adder_4_out));  // open: cin, cout
  Adder #(.width(32)) adder_5 (
    .a({\n32x4乘法器_4_p [7:0], {24{1'b0}}}), .b({\n32x4乘法器_2_p [3:0], {28{1'b0}}}), .out(adder_5_out));  // open: cin, cout
  Adder #(.width(32)) adder_6 (.a(adder_4_out), .b(adder_5_out), .out(adder_6_out));  // open: cin, cout
  Adder #(.width(32)) adder_7 (.a(adder_3_out), .b(adder_6_out), .out(p));  // open: cin, cout
endmodule

module \_32X32乘法器测试电路  (
  input  [31:0] a,
  input  [31:0] b,
  output [31:0] p
);

  \_32X32乘法器  \u_32x32乘法器_1  (.a(a), .b(b), .p(p));
endmodule
