// Logisim project 实验5.circ as structural Verilog: 14 circuits, main circuit 四位二进制可逆计数器
module \四位二进制可逆计数器  (
  input  CLR,
  input  nLD,
  input  A,
  input  CPD,
  input  CPU,
  input  B,
  input  C,
  input  D,
  output QA,
  output QB,
  output QC,
  output QD
);

  wire and_1_out, and_2_out, and_3_out, and_4_out, and_5_out, and_6_out, and_7_out, and_8_out, and_9_out,
       and_10_out, and_11_out, and_12_out, and_13_out, and_14_out, D1_qn, D2_qn, D3_qn, D4_qn, not_1_out,
       not_2_out, not_3_out, not_4_out, not_5_out, not_6_out, not_7_out, not_8_out, or_1_out, or_2_out,
       or_3_out, or_4_out, or_5_out, or_6_out, or_7_out, or_8_out;

  and and_1 (and_1_out, CPU, QA);
  and and_2 (and_2_out, CPD, not_1_out);
  not not_1 (not_1_out, QA);
  not not_2 (not_2_out, QB);
  not not_3 (not_3_out, QC);
  and and_3 (and_3_out, QA, CPU, QB);
  and and_4 (and_4_out, not_1_out, not_2_out, CPD);
  and and_5 (and_5_out, QB, QA, CPU, QC);
  and and_6 (and_6_out, not_2_out, not_1_out, not_3_out, CPD);
  or or_1 (or_1_out, CPD, CPU);
  or or_2 (or_2_out, and_1_out, and_2_out);
  or or_3 (or_3_out, and_3_out, and_4_out);
  or or_4 (or_4_out, and_5_out, and_6_out);
  D_Flip_Flop #(.trigger("falling"), .Pre_Clr_Positions("BELOW_ABOVE"), .NegatePresetClear("false"), .enable("false"), .NewFFLayout("true")) D1 (
    .clk(or_1_out), .D(D1_qn), .Q(QA), .Qn(D1_qn), .preset(and_8_out), .reset(or_5_out));
  D_Flip_Flop #(.trigger("falling"), .Pre_Clr_Positions("BELOW_ABOVE"), .NegatePresetClear("false"), .enable("false"), .NewFFLayout("true")) D2 (
    .clk(or_2_out), .D(D2_qn), .Q(QB), .Qn(D2_qn), .preset(and_10_out), .reset(or_6_out));
  D_Flip_Flop #(.trigger("falling"), .Pre_Clr_Positions("BELOW_ABOVE"), .NegatePresetClear("false"), .enable("false"), .NewFFLayout("true")) D3 (
    .clk(or_3_out), .D(D3_qn), .Q(QC), .Qn(D3_qn), .preset(and_12_out), .reset(or_7_out));
  D_Flip_Flop #(.trigger("falling"), .Pre_Clr_Positions("BELOW_ABOVE"), .NegatePresetClear("false"), .enable("false"), .NewFFLayout("true")) D4 (
    .clk(or_4_out), .D(D4_qn), .Q(QD), .Qn(D4_qn), .preset(and_14_out), .reset(or_8_out));
  or or_5 (or_5_out, CLR, and_7_out);
  or or_6 (or_6_out, CLR, and_9_out);
  or or_7 (or_7_out, CLR, and_11_out);
  or or_8 (or_8_out, CLR, and_13_out);
  not not_4 (not_4_out, nLD);
  and and_7 (and_7_out, not_5_out, not_4_out);
  and and_8 (and_8_out, not_4_out, A);
  and and_9 (and_9_out, not_6_out, not_4_out);
  and and_10 (and_10_out, not_4_out, B);
  and and_11 (and_11_out, not_7_out, not_4_out);
  and and_12 (and_12_out, not_4_out, C);
  and and_13 (and_13_out, not_8_out, not_4_out);
  and and_14 (and_14_out, not_4_out, D);
  not not_5 (not_5_out, A);
  not not_6 (not_6_out, B);
  not not_7 (not_7_out, C);
  not not_8 (not_8_out, D);
endmodule

module \六十进制计数器  (
  input  CPU,
  input  CPD,
  input  Adj,
  input  Clr,
  output Q1D,
  output Q1C,
  output Q1B,
  output Q1A,
  output Q0D,
  output Q0C,
  output Q0B,
  output Q0A,
  output nQcc
);

  wire and_2_out, and_3_out, and_4_out, and_5_out, not_1_out, not_2_out, not_3_out, or_1_out, or_2_out,
       or_3_out;

  and and_1 (nQcc, Q1B, Q1C);
  or or_1 (or_1_out, nQcc, Clr);
  or or_2 (or_2_out, Q1A, Q1B, Q1C, Q0D, Q0C, Q0B, Q0A);
  and and_2 (and_2_out, or_2_out, CPD);
  and and_3 (and_3_out, not_1_out, Q0B, Q0D, not_2_out);
  \四位二进制可逆计数器  \u_四位二进制可逆计数器_1  (
    .CPD(and_5_out), .CPU(and_3_out), .CLR(or_1_out), .nLD(1'b1), .A(1'b1), .QA(Q1A), .B(1'b1), .QB(Q1B),
    .C(1'b1), .QC(Q1C), .D(1'b1), .QD(Q1D));
  not not_1 (not_1_out, Q0C);
  not not_2 (not_2_out, Q0A);
  and and_4 (and_4_out, and_2_out, Adj);
  or or_3 (or_3_out, and_3_out, Clr);
  \四位二进制可逆计数器  \u_四位二进制可逆计数器_2  (
    .CPD(and_4_out), .CPU(CPU), .CLR(or_3_out), .nLD(not_3_out), .A(1'b1), .QA(Q0A), .B(1'b0), .QB(Q0B),
    .C(1'b0), .QC(Q0C), .D(1'b1), .QD(Q0D));
  not not_3 (not_3_out, and_5_out);
  and and_5 (and_5_out, Q0B, Q0A, Q0D, Q0C);
endmodule

module \六十进制计数器测试电路  (
  input  Adj,
  input  Clr
);

  wire CPD_out, CPU_out, \六十进制计数器_1_nqcc ;
  wire [3:0] \六十进制计数器_1_q0a , \六十进制计数器_1_q1a , \四位二进制可逆计数器_1_qa ;

  Button CPU (.out(CPU_out));
  Button CPD (.out(CPD_out));
  Hex_Digit_Display hex_digit_display_1 (.value(\六十进制计数器_1_q1a ));  // open: dp
  Hex_Digit_Display hex_digit_display_2 (.value(\六十进制计数器_1_q0a ));  // open: dp
  \六十进制计数器  \u_六十进制计数器_1  (
    .nQcc(\六十进制计数器_1_nqcc ), .CPU(CPU_out), .CPD(CPD_out), .Adj(Adj), .Clr(Clr), .Q1D(\六十进制计数器_1_q1a [3]),
    .Q1C(\六十进制计数器_1_q1a [2]), .Q1B(\六十进制计数器_1_q1a [1]), .Q1A(\六十进制计数器_1_q1a [0]), .Q0D(\六十进制计数器_1_q0a [3]),
    .Q0C(\六十进制计数器_1_q0a [2]), .Q0B(\六十进制计数器_1_q0a [1]), .Q0A(\六十进制计数器_1_q0a [0]));
  Hex_Digit_Display hex_digit_display_3 (.value(\四位二进制可逆计数器_1_qa ));  // open: dp
  \四位二进制可逆计数器  \u_四位二进制可逆计数器_1  (
    .CPD(1'b0), .CPU(\六十进制计数器_1_nqcc ), .CLR(Clr), .QA(\四位二进制可逆计数器_1_qa [0]), .QB(\四位二进制可逆计数器_1_qa [1]),
    .QC(\四位二进制可逆计数器_1_qa [2]), .QD(\四位二进制可逆计数器_1_qa [3]));  // open: nLD, A, B, C, D
endmodule

module \十二进制计数器或二十四进制的计数器电路  (
  input  Set,
  input  CPU,
  input  Adj,
  input  CPD,
  input  Clr,
  output Q1D,
  output Q1C,
  output Q1B,
  output Q1A,
  output Q0D,
  output Q0C,
  output Q0B,
  output Q0A,
  output nQcc_12,
  output nQcc_24
);

  wire or_1_out, or_2_out;
  wire [7:0] \六十进制计数器_1_q0a , \六十进制计数器_2_q0a ;

  \六十进制计数器  \u_六十进制计数器_1  (
    .CPU(CPU), .CPD(CPD), .Adj(Adj), .Clr(or_1_out), .Q1D(\六十进制计数器_1_q0a [7]), .Q1C(\六十进制计数器_1_q0a [6]),
    .Q1B(\六十进制计数器_1_q0a [5]), .Q1A(\六十进制计数器_1_q0a [4]), .Q0D(\六十进制计数器_1_q0a [3]), .Q0C(\六十进制计数器_1_q0a [2]),
    .Q0B(\六十进制计数器_1_q0a [1]), .Q0A(\六十进制计数器_1_q0a [0]));  // open: nQcc
  Multiplexer #(.select(1), .width(8), .disabled("Z"), .enable("false")) multiplexer_1 (
    .in0(\六十进制计数器_1_q0a ), .in1(\六十进制计数器_2_q0a ), .out({Q1D, Q1C, Q1B, Q1A, Q0D, Q0C, Q0B, Q0A}), .sel(Set));
  or or_1 (or_1_out, nQcc_12, Clr);
  and and_1 (nQcc_12, \六十进制计数器_1_q0a [1], \六十进制计数器_1_q0a [4]);
  \六十进制计数器  \u_六十进制计数器_2  (
    .CPU(CPU), .CPD(CPD), .Adj(Adj), .Clr(or_2_out), .Q1D(\六十进制计数器_2_q0a [7]), .Q1C(\六十进制计数器_2_q0a [6]),
    .Q1B(\六十进制计数器_2_q0a [5]), .Q1A(\六十进制计数器_2_q0a [4]), .Q0D(\六十进制计数器_2_q0a [3]), .Q0C(\六十进制计数器_2_q0a [2]),
    .Q0B(\六十进制计数器_2_q0a [1]), .Q0A(\六十进制计数器_2_q0a [0]));  // open: nQcc
  or or_2 (or_2_out, nQcc_24, Clr);
  and and_2 (nQcc_24, \六十进制计数器_2_q0a [2], \六十进制计数器_2_q0a [5]);
endmodule

module \十二进制计数器或二十四进制的计数器测试电路  (
  input  Adj,
  input  in_2,
  input  in_3
);

  wire and_1_out, and_2_out, CPD_out, CPU_out, not_1_out, or_1_out, \十二进制计数器或二十四进制的计数器电路_1_nqcc_12 ,
       \十二进制计数器或二十四进制的计数器电路_1_nqcc_24 ;
  wire [3:0] \十二进制计数器或二十四进制的计数器电路_1_q0a , \十二进制计数器或二十四进制的计数器电路_1_q1a , \四位二进制可逆计数器_1_qa ;

  Button CPU (.out(CPU_out));
  Button CPD (.out(CPD_out));
  Hex_Digit_Display hex_digit_display_1 (.value(\十二进制计数器或二十四进制的计数器电路_1_q1a ));  // open: dp
  Hex_Digit_Display hex_digit_display_2 (.value(\十二进制计数器或二十四进制的计数器电路_1_q0a ));  // open: dp
  not not_1 (not_1_out, in_2);
  \十二进制计数器或二十四进制的计数器电路  \u_十二进制计数器或二十四进制的计数器电路_1  (
    .Set(in_2), .CPU(CPU_out), .Adj(Adj), .CPD(CPD_out), .Clr(in_3),
    .nQcc_24(\十二进制计数器或二十四进制的计数器电路_1_nqcc_24 ), .Q1D(\十二进制计数器或二十四进制的计数器电路_1_q1a [3]),
    .Q1C(\十二进制计数器或二十四进制的计数器电路_1_q1a [2]), .Q1B(\十二进制计数器或二十四进制的计数器电路_1_q1a [1]),
    .Q1A(\十二进制计数器或二十四进制的计数器电路_1_q1a [0]), .Q0D(\十二进制计数器或二十四进制的计数器电路_1_q0a [3]),
    .Q0C(\十二进制计数器或二十四进制的计数器电路_1_q0a [2]), .Q0B(\十二进制计数器或二十四进制的计数器电路_1_q0a [1]),
    .Q0A(\十二进制计数器或二十四进制的计数器电路_1_q0a [0]), .nQcc_12(\十二进制计数器或二十四进制的计数器电路_1_nqcc_12 ));
  and and_1 (and_1_out, \十二进制计数器或二十四进制的计数器电路_1_nqcc_24 , in_2);
  or or_1 (or_1_out, and_1_out, and_2_out);
  and and_2 (and_2_out, not_1_out, \十二进制计数器或二十四进制的计数器电路_1_nqcc_12 );
  Hex_Digit_Display hex_digit_display_3 (.value(\四位二进制可逆计数器_1_qa ));  // open: dp
  \四位二进制可逆计数器  \u_四位二进制可逆计数器_1  (
    .CPD(1'b0), .CPU(or_1_out), .CLR(in_3), .QA(\四位二进制可逆计数器_1_qa [0]), .QB(\四位二进制可逆计数器_1_qa [1]),
    .QC(\四位二进制可逆计数器_1_qa [2]), .QD(\四位二进制可逆计数器_1_qa [3]));  // open: nLD, A, B, C, D
endmodule

module \上下午文字显示的电路  (
  input  AM_PM,
  input  TT,
  output [4:0] out_3,
  output [4:0] out_4,
  output [4:0] out_5,
  output [4:0] out_6
);

  wire [19:0] multiplexer_1_out;

  Multiplexer #(.select(1), .width(20), .disabled("Z"), .enable("false")) multiplexer_1 (
    .in0(20'h97e1), .in1(20'h853f0), .out(multiplexer_1_out), .sel(AM_PM));
  Multiplexer #(.select(1), .width(20), .disabled("Z"), .enable("false")) multiplexer_2 (
    .in0({20{1'b0}}), .in1(multiplexer_1_out), .out({out_6, out_5, out_4, out_3}), .sel(TT));
endmodule

module \上下午文字显示测试电路  (
  input  AM_PM,
  input  TT
);

  wire [4:0] \上下午文字显示的电路_1_out_3 , \上下午文字显示的电路_1_out_4 , \上下午文字显示的电路_1_out_5 , \上下午文字显示的电路_1_out_6 ;

  DotMatrix #(.inputtype("column"), .matrixcols(4), .matrixrows(5), .persist(0), .dotshape("square")) dotmatrix_1 (
    .col0(\上下午文字显示的电路_1_out_3 ), .col1(\上下午文字显示的电路_1_out_4 ), .col2(\上下午文字显示的电路_1_out_5 ),
    .col3(\上下午文字显示的电路_1_out_6 ));
  \上下午文字显示的电路  \u_上下午文字显示的电路_1  (
    .out_3(\上下午文字显示的电路_1_out_3 ), .out_4(\上下午文字显示的电路_1_out_4 ), .out_5(\上下午文字显示的电路_1_out_5 ),
    .out_6(\上下午文字显示的电路_1_out_6 ), .AM_PM(AM_PM), .TT(TT));
endmodule

module \电子钟整点报时电路  (
  input  CPU,
  input  Set,
  input  CPD,
  input  Adj,
  input  Clr,
  output [3:0] out_6,
  output [3:0] out_7,
  output [3:0] out_8,
  output [3:0] out_9,
  output [3:0] out_10,
  output [3:0] out_11,
  output out_12
);

  wire \六十进制计数器_1_nqcc , \六十进制计数器_2_nqcc ;

  \六十进制计数器  \u_六十进制计数器_1  (
    .nQcc(\六十进制计数器_1_nqcc ), .CPU(CPU), .CPD(CPD), .Adj(Adj), .Clr(Clr), .Q1D(out_8[3]), .Q1C(out_8[2]),
    .Q1B(out_8[1]), .Q1A(out_8[0]), .Q0D(out_9[3]), .Q0C(out_9[2]), .Q0B(out_9[1]), .Q0A(out_9[0]));
  \六十进制计数器  \u_六十进制计数器_2  (
    .nQcc(\六十进制计数器_2_nqcc ), .CPU(\六十进制计数器_1_nqcc ), .CPD(CPD), .Adj(Adj), .Clr(Clr), .Q1D(out_6[3]),
    .Q1C(out_6[2]), .Q1B(out_6[1]), .Q1A(out_6[0]), .Q0D(out_7[3]), .Q0C(out_7[2]), .Q0B(out_7[1]),
    .Q0A(out_7[0]));
  \十二进制计数器或二十四进制的计数器电路  \u_十二进制计数器或二十四进制的计数器电路_1  (
    .Set(Set), .CPU(\六十进制计数器_2_nqcc ), .Adj(Adj), .CPD(CPD), .Clr(Clr), .Q1D(out_10[3]), .Q1C(out_10[2]),
    .Q1B(out_10[1]), .Q1A(out_10[0]), .Q0D(out_11[3]), .Q0C(out_11[2]), .Q0B(out_11[1]), .Q0A(out_11[0]));  // open: nQcc_24, nQcc_12
  and and_1 (out_12, out_7[0], out_7[3], out_6[0], out_6[2], out_8[0], out_8[2]);
endmodule

module \电子钟整点报时电路测试电路  (
  input  Adj,
  input  Set,
  input  CPD,
  input  Clr
);

  wire \电子钟整点报时电路_1_out_12 , \计时_out ;
  wire [3:0] \电子钟整点报时电路_1_out_6 , \电子钟整点报时电路_1_out_7 , \电子钟整点报时电路_1_out_8 , \电子钟整点报时电路_1_out_9 ,
       \电子钟整点报时电路_1_out_10 , \电子钟整点报时电路_1_out_11 ;

  Hex_Digit_Display hex_digit_display_1 (.value(\电子钟整点报时电路_1_out_10 ));  // open: dp
  Clock #(.highDuration(1), .lowDuration(1)) \u_计时  (.out(\计时_out ));
  Hex_Digit_Display hex_digit_display_2 (.value(\电子钟整点报时电路_1_out_6 ));  // open: dp
  Hex_Digit_Display hex_digit_display_3 (.value(\电子钟整点报时电路_1_out_11 ));  // open: dp
  Hex_Digit_Display hex_digit_display_4 (.value(\电子钟整点报时电路_1_out_7 ));  // open: dp
  \电子钟整点报时电路  \u_电子钟整点报时电路_1  (
    .CPU(\计时_out ), .CPD(CPD), .Adj(Adj), .Clr(Clr), .out_12(\电子钟整点报时电路_1_out_12 ), .Set(Set),
    .out_8(\电子钟整点报时电路_1_out_8 ), .out_9(\电子钟整点报时电路_1_out_9 ), .out_6(\电子钟整点报时电路_1_out_6 ),
    .out_7(\电子钟整点报时电路_1_out_7 ), .out_10(\电子钟整点报时电路_1_out_10 ), .out_11(\电子钟整点报时电路_1_out_11 ));
  Hex_Digit_Display hex_digit_display_5 (.value(\电子钟整点报时电路_1_out_8 ));  // open: dp
  Hex_Digit_Display hex_digit_display_6 (.value(\电子钟整点报时电路_1_out_9 ));  // open: dp
  LED #(.active("true")) \u_报时  (.in(\电子钟整点报时电路_1_out_12 ));
endmodule

module \秒脉冲产生电路  (
  input  in_1,
  output out_2
);

  \四位二进制可逆计数器  \u_四位二进制可逆计数器_1  (
    .CPD(1'b0), .CPU(in_1), .CLR(out_2), .nLD(1'b1), .A(1'b0), .B(1'b0), .C(1'b0), .QC(out_2), .D(1'b0));  // open: QA, QB, QD
endmodule

module \多功能数字钟  (
  input  Alarm,
  input  Adj0,
  input  Adj1,
  input  CP,
  input  CPU,
  input  CPD,
  input  Set,
  input  Clr,
  output [3:0] out_9,
  output [3:0] out_10,
  output [3:0] out_11,
  output [3:0] out_12,
  output [3:0] out_13,
  output [3:0] out_14,
  output \定点报时 ,
  output [4:0] out_16,
  output [4:0] out_17,
  output [4:0] out_18,
  output [4:0] out_19,
  output \闹钟 
);

  wire not_1_out, \秒脉冲产生电路_1_out_2 ;

  \秒脉冲产生电路  \u_秒脉冲产生电路_1  (.in_1(CP), .out_2(\秒脉冲产生电路_1_out_2 ));
  \闹钟  \u_闹钟_1  (
    .Alarm(Alarm), .CP(\秒脉冲产生电路_1_out_2 ), .Adj0(Adj0), .Adj1(Adj1), .CPD(CPD), .CPU(CPU), .Clr(Clr),
    .\闹钟 (\闹钟 ), .Set(Set), .\秒1 (out_13), .\秒0 (out_14), .\分1 (out_11), .\分0 (out_12), .\时1 (out_9),
    .\时0 (out_10), .out_16(out_19), .out_17(out_18), .out_18(out_17), .out_19(out_16));
  not not_1 (not_1_out, Alarm);
  and and_1 (\定点报时 , out_11[0], out_11[2], out_12[0], out_12[3], out_13[0], out_13[2], not_1_out);
endmodule

module \多功能数字钟测试电路  (
  input  Alarm,
  input  Adj0,
  input  Adj1,
  input  Set
);

  wire Clr_out, CP_out, CPD_out, CPU_out, \多功能数字钟_1_定点报时 , \多功能数字钟_1_闹钟 ;
  wire [3:0] \多功能数字钟_1_out_9 , \多功能数字钟_1_out_10 , \多功能数字钟_1_out_11 , \多功能数字钟_1_out_12 , \多功能数字钟_1_out_13 ,
       \多功能数字钟_1_out_14 ;
  wire [4:0] \多功能数字钟_1_out_16 , \多功能数字钟_1_out_17 , \多功能数字钟_1_out_18 , \多功能数字钟_1_out_19 ;

  DotMatrix #(.inputtype("column"), .matrixcols(4), .matrixrows(5), .persist(0), .dotshape("square")) dotmatrix_1 (
    .col0(\多功能数字钟_1_out_19 ), .col1(\多功能数字钟_1_out_18 ), .col2(\多功能数字钟_1_out_17 ), .col3(\多功能数字钟_1_out_16 ));
  Hex_Digit_Display hex_digit_display_1 (.value(\多功能数字钟_1_out_9 ));  // open: dp
  Clock #(.highDuration(1), .lowDuration(1)) CP (.out(CP_out));
  Hex_Digit_Display hex_digit_display_2 (.value(\多功能数字钟_1_out_10 ));  // open: dp
  Button CPU (.out(CPU_out));
  Button CPD (.out(CPD_out));
  Hex_Digit_Display hex_digit_display_3 (.value(\多功能数字钟_1_out_11 ));  // open: dp
  Hex_Digit_Display hex_digit_display_4 (.value(\多功能数字钟_1_out_12 ));  // open: dp
  \多功能数字钟  \u_多功能数字钟_1  (
    .out_16(\多功能数字钟_1_out_16 ), .out_17(\多功能数字钟_1_out_17 ), .out_18(\多功能数字钟_1_out_18 ),
    .out_19(\多功能数字钟_1_out_19 ), .Alarm(Alarm), .Adj0(Adj0), .Adj1(Adj1), .\定点报时 (\多功能数字钟_1_定点报时 ),
    .\闹钟 (\多功能数字钟_1_闹钟 ), .out_9(\多功能数字钟_1_out_9 ), .out_10(\多功能数字钟_1_out_10 ), .out_11(\多功能数字钟_1_out_11 ),
    .out_12(\多功能数字钟_1_out_12 ), .out_13(\多功能数字钟_1_out_13 ), .out_14(\多功能数字钟_1_out_14 ), .CP(CP_out),
    .CPU(CPU_out), .CPD(CPD_out), .Set(Set), .Clr(Clr_out));
  Button Clr (.out(Clr_out));
  Hex_Digit_Display hex_digit_display_5 (.value(\多功能数字钟_1_out_13 ));  // open: dp
  Hex_Digit_Display hex_digit_display_6 (.value(\多功能数字钟_1_out_14 ));  // open: dp
  LED #(.active("true")) \u_闹钟  (.in(\多功能数字钟_1_闹钟 ));
  LED #(.active("true")) \u_定时报点  (.in(\多功能数字钟_1_定点报时 ));
endmodule

module \闹钟  (
  input  Alarm,
  input  CP,
  input  Set,
  input  Adj0,
  input  Adj1,
  input  CPD,
  input  CPU,
  input  Clr,
  output [3:0] \秒1 ,
  output [3:0] \秒0 ,
  output [3:0] \分1 ,
  output [3:0] \分0 ,
  output [3:0] \时1 ,
  output [3:0] \时0 ,
  output \闹钟 ,
  output [4:0] out_16,
  output [4:0] out_17,
  output [4:0] out_18,
  output [4:0] out_19
);

  wire and_1_out, and_2_out, and_3_out, and_4_out, and_5_out, and_6_out, and_7_out, and_8_out, and_9_out,
       and_10_out, and_11_out, and_12_out, comparator_1_lt, multiplexer_1_out, multiplexer_2_out,
       multiplexer_4_out, multiplexer_5_out, multiplexer_6_out, not_1_out, not_2_out, not_3_out, not_4_out,
       not_5_out, subtractor_1_bout, \六十进制计数器_1_nqcc , \六十进制计数器_3_nqcc , \十二进制计数器或二十四进制的计数器电路_1_nqcc_12 ,
       \十二进制计数器或二十四进制的计数器电路_2_nqcc_12 ;
  wire [3:0] \六十进制计数器_1_q0a , \六十进制计数器_1_q1a , \六十进制计数器_2_q0a , \六十进制计数器_3_q0a , \六十进制计数器_3_q1a ,
       \十二进制计数器或二十四进制的计数器电路_2_q0a , \十二进制计数器或二十四进制的计数器电路_2_q1a ;
  wire [11:0] \六十进制计数器_2_q1a ;
  wire [24:0] subtractor_1_out;
  wire [24:24] \四位二进制可逆计数器_1_qa , \四位二进制可逆计数器_2_qa ;

  not not_1 (not_1_out, Alarm);
  and and_1 (and_1_out, Clr, Alarm);
  and and_2 (and_2_out, not_1_out, Clr);
  \六十进制计数器  \u_六十进制计数器_1  (
    .nQcc(\六十进制计数器_1_nqcc ), .CPU(CP), .CPD(1'b0), .Adj(1'b0), .Clr(and_2_out), .Q1D(\六十进制计数器_1_q1a [3]),
    .Q1C(\六十进制计数器_1_q1a [2]), .Q1B(\六十进制计数器_1_q1a [1]), .Q1A(\六十进制计数器_1_q1a [0]), .Q0D(\六十进制计数器_1_q0a [3]),
    .Q0C(\六十进制计数器_1_q0a [2]), .Q0B(\六十进制计数器_1_q0a [1]), .Q0A(\六十进制计数器_1_q0a [0]));
  and and_3 (and_3_out, CPU, Adj1, Alarm);
  and and_4 (and_4_out, CPD, Adj1, Alarm);
  and and_5 (and_5_out, Alarm, Adj1);
  Multiplexer #(.select(1), .width(1), .disabled("Z"), .enable("false")) multiplexer_1 (
    .in0(1'b0), .in1(and_3_out), .out(multiplexer_1_out), .sel(Adj1));
  Multiplexer #(.select(1), .width(1), .disabled("Z"), .enable("false")) multiplexer_2 (
    .in0(\六十进制计数器_1_nqcc ), .in1(and_6_out), .out(multiplexer_2_out), .sel(Adj0));
  and and_6 (and_6_out, CPU, Adj1, Adj0);
  and and_7 (and_7_out, Adj1, Adj0);
  Multiplexer #(.select(1), .width(24), .disabled("Z"), .enable("false")) multiplexer_3 (
    .in0({\六十进制计数器_1_q0a , \六十进制计数器_1_q1a , \六十进制计数器_3_q0a , \六十进制计数器_3_q1a , \十二进制计数器或二十四进制的计数器电路_2_q0a , \十二进制计数器或二十四进制的计数器电路_2_q1a }),
    .in1({{8{1'b0}}, \六十进制计数器_2_q0a , \六十进制计数器_2_q1a }), .out({\秒0 , \秒1 , \分0 , \分1 , \时0 , \时1 }),
    .sel(Alarm));
  \六十进制计数器  \u_六十进制计数器_2  (
    .CPU(multiplexer_1_out), .CPD(and_4_out), .Adj(and_5_out), .Clr(and_1_out), .Q1D(\六十进制计数器_2_q1a [11]),
    .Q1C(\六十进制计数器_2_q1a [10]), .Q1B(\六十进制计数器_2_q1a [9]), .Q1A(\六十进制计数器_2_q1a [8]), .Q0D(\六十进制计数器_2_q0a [3]),
    .Q0C(\六十进制计数器_2_q0a [2]), .Q0B(\六十进制计数器_2_q0a [1]), .Q0A(\六十进制计数器_2_q0a [0]));  // open: nQcc
  \六十进制计数器  \u_六十进制计数器_3  (
    .nQcc(\六十进制计数器_3_nqcc ), .CPU(multiplexer_2_out), .CPD(CPD), .Adj(and_7_out), .Clr(and_2_out),
    .Q1D(\六十进制计数器_3_q1a [3]), .Q1C(\六十进制计数器_3_q1a [2]), .Q1B(\六十进制计数器_3_q1a [1]), .Q1A(\六十进制计数器_3_q1a [0]),
    .Q0D(\六十进制计数器_3_q0a [3]), .Q0C(\六十进制计数器_3_q0a [2]), .Q0B(\六十进制计数器_3_q0a [1]), .Q0A(\六十进制计数器_3_q0a [0]));
  not not_2 (not_2_out, Adj1);
  and and_8 (and_8_out, CPU, not_2_out, Alarm);
  and and_9 (and_9_out, CPD, not_2_out, Alarm);
  and and_10 (and_10_out, not_2_out, Alarm);
  Multiplexer #(.select(1), .width(1), .disabled("Z"), .enable("false")) multiplexer_4 (
    .in0(and_8_out), .in1(1'b0), .out(multiplexer_4_out), .sel(Adj1));
  Multiplexer #(.select(1), .width(1), .disabled("Z"), .enable("false")) multiplexer_5 (
    .in0(\六十进制计数器_3_nqcc ), .in1(and_11_out), .out(multiplexer_5_out), .sel(Adj0));
  not not_3 (not_3_out, Adj1);
  and and_11 (and_11_out, CPU, Adj0, not_3_out);
  \十二进制计数器或二十四进制的计数器电路  \u_十二进制计数器或二十四进制的计数器电路_1  (
    .Set(Set), .CPU(multiplexer_4_out), .Adj(and_10_out), .CPD(and_9_out), .Clr(and_1_out),
    .Q1D(\六十进制计数器_2_q1a [3]), .Q1C(\六十进制计数器_2_q1a [2]), .Q1B(\六十进制计数器_2_q1a [1]), .Q1A(\六十进制计数器_2_q1a [0]),
    .Q0D(\六十进制计数器_2_q1a [7]), .Q0C(\六十进制计数器_2_q1a [6]), .Q0B(\六十进制计数器_2_q1a [5]), .Q0A(\六十进制计数器_2_q1a [4]),
    .nQcc_12(\十二进制计数器或二十四进制的计数器电路_1_nqcc_12 ));  // open: nQcc_24
  and and_12 (and_12_out, Adj0, not_3_out);
  \十二进制计数器或二十四进制的计数器电路  \u_十二进制计数器或二十四进制的计数器电路_2  (
    .Set(Set), .CPU(multiplexer_5_out), .Adj(and_12_out), .CPD(CPD), .Clr(and_2_out),
    .Q1D(\十二进制计数器或二十四进制的计数器电路_2_q1a [3]), .Q1C(\十二进制计数器或二十四进制的计数器电路_2_q1a [2]),
    .Q1B(\十二进制计数器或二十四进制的计数器电路_2_q1a [1]), .Q1A(\十二进制计数器或二十四进制的计数器电路_2_q1a [0]),
    .Q0D(\十二进制计数器或二十四进制的计数器电路_2_q0a [3]), .Q0C(\十二进制计数器或二十四进制的计数器电路_2_q0a [2]),
    .Q0B(\十二进制计数器或二十四进制的计数器电路_2_q0a [1]), .Q0A(\十二进制计数器或二十四进制的计数器电路_2_q0a [0]),
    .nQcc_12(\十二进制计数器或二十四进制的计数器电路_2_nqcc_12 ));  // open: nQcc_24
  Subtractor #(.width(25)) subtractor_1 (
    .a({\四位二进制可逆计数器_1_qa [24], \十二进制计数器或二十四进制的计数器电路_2_q1a , \十二进制计数器或二十四进制的计数器电路_2_q0a , \六十进制计数器_3_q1a , \六十进制计数器_3_q0a , \六十进制计数器_1_q1a , \六十进制计数器_1_q0a }),
    .b({\四位二进制可逆计数器_2_qa [24], \六十进制计数器_2_q1a [3:0], \六十进制计数器_2_q1a [7:4], \六十进制计数器_2_q1a [11:8], \六十进制计数器_2_q0a , {8{1'b0}}}),
    .out(subtractor_1_out), .bout(subtractor_1_bout));  // open: bin
  not not_4 (not_4_out, subtractor_1_bout);
  Comparator #(.width(25), .mode("twosComplement")) comparator_1 (
    .a(subtractor_1_out), .b(25'ha), .lt(comparator_1_lt));  // open: gt, eq
  and and_13 (\闹钟 , comparator_1_lt, not_4_out);
  not not_5 (not_5_out, Set);
  \四位二进制可逆计数器  \u_四位二进制可逆计数器_1  (
    .CPD(1'b0), .CPU(\十二进制计数器或二十四进制的计数器电路_2_nqcc_12 ), .CLR(and_2_out), .nLD(1'b1), .A(1'b1),
    .QA(\四位二进制可逆计数器_1_qa [24]), .B(1'b1), .C(1'b1), .D(1'b1));  // open: QB, QC, QD
  \四位二进制可逆计数器  \u_四位二进制可逆计数器_2  (
    .CPD(1'b0), .CPU(\十二进制计数器或二十四进制的计数器电路_1_nqcc_12 ), .CLR(and_1_out), .nLD(1'b1), .A(1'b1),
    .QA(\四位二进制可逆计数器_2_qa [24]), .B(1'b1), .C(1'b1), .D(1'b1));  // open: QB, QC, QD
  Multiplexer #(.select(1), .width(1), .disabled("Z"), .enable("false")) multiplexer_6 (
    .in0(\四位二进制可逆计数器_1_qa [24]), .in1(\四位二进制可逆计数器_2_qa [24]), .out(multiplexer_6_out), .sel(Alarm));
  \上下午文字显示的电路  \u_上下午文字显示的电路_1  (
    .out_3(out_16), .out_4(out_17), .out_5(out_18), .out_6(out_19), .AM_PM(multiplexer_6_out), .TT(not_5_out));
endmodule

module \闹钟测试  (
  input  Alarm,
  input  Adj0,
  input  Adj1,
  input  Set
);

  wire clock_1_out, Clr_out, CPD_out, CPU_out, \闹钟_1_闹钟 ;
  wire [3:0] \闹钟_1_分0 , \闹钟_1_分1 , \闹钟_1_时0 , \闹钟_1_时1 , \闹钟_1_秒0 , \闹钟_1_秒1 ;
  wire [4:0] \闹钟_1_out_16 , \闹钟_1_out_17 , \闹钟_1_out_18 , \闹钟_1_out_19 ;

  Clock #(.highDuration(1), .lowDuration(1)) clock_1 (.out(clock_1_out));
  Button CPU (.out(CPU_out));
  Button CPD (.out(CPD_out));
  DotMatrix #(.inputtype("column"), .matrixcols(4), .matrixrows(5), .persist(0), .dotshape("square")) dotmatrix_1 (
    .col0(\闹钟_1_out_16 ), .col1(\闹钟_1_out_17 ), .col2(\闹钟_1_out_18 ), .col3(\闹钟_1_out_19 ));
  Hex_Digit_Display hex_digit_display_1 (.value(\闹钟_1_时1 ));  // open: dp
  Hex_Digit_Display hex_digit_display_2 (.value(\闹钟_1_时0 ));  // open: dp
  Hex_Digit_Display hex_digit_display_3 (.value(\闹钟_1_分0 ));  // open: dp
  Hex_Digit_Display hex_digit_display_4 (.value(\闹钟_1_分1 ));  // open: dp
  \闹钟  \u_闹钟_1  (
    .Alarm(Alarm), .CP(clock_1_out), .Adj0(Adj0), .Adj1(Adj1), .CPD(CPD_out), .CPU(CPU_out), .Clr(Clr_out),
    .\闹钟 (\闹钟_1_闹钟 ), .Set(Set), .\秒1 (\闹钟_1_秒1 ), .\秒0 (\闹钟_1_秒0 ), .\分1 (\闹钟_1_分1 ), .\分0 (\闹钟_1_分0 ),
    .\时1 (\闹钟_1_时1 ), .\时0 (\闹钟_1_时0 ), .out_16(\闹钟_1_out_16 ), .out_17(\闹钟_1_out_17 ),
    .out_18(\闹钟_1_out_18 ), .out_19(\闹钟_1_out_19 ));
  Hex_Digit_Display hex_digit_display_5 (.value(\闹钟_1_秒1 ));  // open: dp
  LED #(.active("true")) \u_闹钟_2  (.in(\闹钟_1_闹钟 ));
  Button Clr (.out(Clr_out));
  Hex_Digit_Display hex_digit_display_6 (.value(\闹钟_1_秒0 ));  // open: dp
endmodule
