// Logisim project 实验6.circ as structural Verilog: 7 circuits, main circuit sqrX
module sqrX (
  input  [31:0] a,
  input  [31:0] b,
  input  [31:0] c,
  input  [31:0] d,
  output [31:0] a_prime,
  output [31:0] b_prime,
  output [31:0] c_prime,
  output [31:0] d_prime
);

  wire [31:0] multiplier_1_out, multiplier_2_out, multiplier_3_out, multiplier_4_out, multiplier_5_out,
       multiplier_6_out, multiplier_7_out;

  Multiplier #(.width(32)) multiplier_1 (.a(a), .b(a), .out(multiplier_1_out));  // open: cin, cout
  Multiplier #(.width(32)) multiplier_2 (.a(b), .b(c), .out(multiplier_2_out));  // open: cin, cout
  Multiplier #(.width(32)) multiplier_3 (.a(a), .b(b), .out(multiplier_3_out));  // open: cin, cout
  Multiplier #(.width(32)) multiplier_4 (.a(b), .b(d), .out(multiplier_4_out));  // open: cin, cout
  Multiplier #(.width(32)) multiplier_5 (.a(c), .b(a), .out(multiplier_5_out));  // open: cin, cout
  Multiplier #(.width(32)) multiplier_6 (.a(d), .b(c), .out(multiplier_6_out));  // open: cin, cout
  Multiplier #(.width(32)) multiplier_7 (.a(d), .b(d), .out(multiplier_7_out));  // open: cin, cout
  Adder #(.width(32)) adder_1 (.a(multiplier_1_out), .b(multiplier_2_out), .out(a_prime));  // open: cin, cout
  Adder #(.width(32)) adder_2 (.a(multiplier_3_out), .b(multiplier_4_out), .out(b_prime));  // open: cin, cout
  Adder #(.width(32)) adder_3 (.a(multiplier_5_out), .b(multiplier_6_out), .out(c_prime));  // open: cin, cout
  Adder #(.width(32)) adder_4 (.a(multiplier_2_out), .b(multiplier_7_out), .out(d_prime));  // open: cin, cout
endmodule

module sqrX_A (
  input  [31:0] a,
  input  [31:0] b,
  input  [31:0] c,
  input  [31:0] d,
  output [31:0] a_prime_prime,
  output [31:0] b_prime_prime,
  output [31:0] c_prime_prime,
  output [31:0] d_prime_prime
);

  wire [31:0] adder_2_out, adder_4_out, multiplier_1_out, multiplier_2_out, multiplier_3_out,
       multiplier_4_out, multiplier_5_out, multiplier_6_out, multiplier_7_out;

  Multiplier #(.width(32)) multiplier_1 (.a(a), .b(b), .out(multiplier_1_out));  // open: cin, cout
  Multiplier #(.width(32)) multiplier_2 (.a(b), .b(d), .out(multiplier_2_out));  // open: cin, cout
  Multiplier #(.width(32)) multiplier_3 (.a(a), .b(a), .out(multiplier_3_out));  // open: cin, cout
  Multiplier #(.width(32)) multiplier_4 (.a(b), .b(c), .out(multiplier_4_out));  // open: cin, cout
  Multiplier #(.width(32)) multiplier_5 (.a(d), .b(d), .out(multiplier_5_out));  // open: cin, cout
  Multiplier #(.width(32)) multiplier_6 (.a(a), .b(c), .out(multiplier_6_out));  // open: cin, cout
  Multiplier #(.width(32)) multiplier_7 (.a(d), .b(c), .out(multiplier_7_out));  // open: cin, cout
  Adder #(.width(32)) adder_1 (.a(multiplier_1_out), .b(multiplier_2_out), .out(a_prime_prime));  // open: cin, cout
  Adder #(.width(32)) adder_2 (.a(multiplier_3_out), .b(multiplier_4_out), .out(adder_2_out));  // open: cin, cout
  Adder #(.width(32)) adder_3 (.a(multiplier_4_out), .b(multiplier_5_out), .out(c_prime_prime));  // open: cin, cout
  Adder #(.width(32)) adder_4 (.a(multiplier_6_out), .b(multiplier_7_out), .out(adder_4_out));  // open: cin, cout
  Adder #(.width(32)) adder_5 (.a(a_prime_prime), .b(adder_2_out), .out(b_prime_prime));  // open: cin, cout
  Adder #(.width(32)) adder_6 (.a(c_prime_prime), .b(adder_4_out), .out(d_prime_prime));  // open: cin, cout
endmodule

module \Fibonacci数显示模块  (
  input  [31:0] Fi,
  output [3:0] D0,
  output [3:0] D1,
  output [3:0] D2,
  output [3:0] D3,
  output [3:0] D4,
  output [3:0] D5,
  output [3:0] D6,
  output [3:0] D7,
  output [3:0] D8,
  output [3:0] D9
);

  wire [3:0] divider_1_rem, divider_1_rem_2, divider_1_rem_3, divider_1_rem_4, divider_1_rem_5,
       divider_1_rem_6, divider_1_rem_7, divider_2_rem, divider_2_rem_2, divider_2_rem_3, divider_2_rem_4,
       divider_2_rem_5, divider_2_rem_6, divider_2_rem_7, divider_3_rem, divider_3_rem_2, divider_3_rem_3,
       divider_3_rem_4, divider_3_rem_5, divider_3_rem_6, divider_3_rem_7, divider_4_rem, divider_4_rem_2,
       divider_4_rem_3, divider_4_rem_4, divider_4_rem_5, divider_4_rem_6, divider_4_rem_7, divider_5_rem,
       divider_5_rem_2, divider_5_rem_3, divider_5_rem_4, divider_5_rem_5, divider_5_rem_6, divider_5_rem_7,
       divider_6_rem, divider_6_rem_2, divider_6_rem_3, divider_6_rem_4, divider_6_rem_5, divider_6_rem_6,
       divider_6_rem_7, divider_7_rem, divider_7_rem_2, divider_7_rem_3, divider_7_rem_4, divider_7_rem_5,
       divider_7_rem_6, divider_7_rem_7, divider_8_rem, divider_8_rem_2, divider_8_rem_3, divider_8_rem_4,
       divider_8_rem_5, divider_8_rem_6, divider_8_rem_7, divider_9_rem, divider_9_rem_2, divider_9_rem_3,
       divider_9_rem_4, divider_9_rem_5, divider_9_rem_6, divider_9_rem_7, divider_10_rem, divider_10_rem_2,
       divider_10_rem_3, divider_10_rem_4, divider_10_rem_5, divider_10_rem_6, divider_10_rem_7;
  wire [31:0] divider_1_out, divider_2_out, divider_3_out, divider_4_out, divider_5_out, divider_6_out,
       divider_7_out, divider_8_out, divider_9_out;

  Divider #(.width(32)) divider_1 (
    .a(Fi), .b(32'ha), .out(divider_1_out),
    .rem({divider_1_rem_7, divider_1_rem_6, divider_1_rem_5, divider_1_rem_4, divider_1_rem_3, divider_1_rem_2, divider_1_rem, D0}));  // open: upper
  Divider #(.width(32)) divider_2 (
    .a(divider_9_out), .b(32'ha), .out(divider_2_out),
    .rem({divider_2_rem_7, divider_2_rem_6, divider_2_rem_5, divider_2_rem_4, divider_2_rem_3, divider_2_rem_2, divider_2_rem, D5}));  // open: upper
  Divider #(.width(32)) divider_3 (
    .a(divider_1_out), .b(32'ha), .out(divider_3_out),
    .rem({divider_3_rem_7, divider_3_rem_6, divider_3_rem_5, divider_3_rem_4, divider_3_rem_3, divider_3_rem_2, divider_3_rem, D1}));  // open: upper
  Divider #(.width(32)) divider_4 (
    .a(divider_2_out), .b(32'ha), .out(divider_4_out),
    .rem({divider_4_rem_7, divider_4_rem_6, divider_4_rem_5, divider_4_rem_4, divider_4_rem_3, divider_4_rem_2, divider_4_rem, D6}));  // open: upper
  Divider #(.width(32)) divider_5 (
    .a(divider_3_out), .b(32'ha), .out(divider_5_out),
    .rem({divider_5_rem_7, divider_5_rem_6, divider_5_rem_5, divider_5_rem_4, divider_5_rem_3, divider_5_rem_2, divider_5_rem, D2}));  // open: upper
  Divider #(.width(32)) divider_6 (
    .a(divider_4_out), .b(32'ha), .out(divider_6_out),
    .rem({divider_6_rem_7, divider_6_rem_6, divider_6_rem_5, divider_6_rem_4, divider_6_rem_3, divider_6_rem_2, divider_6_rem, D7}));  // open: upper
  Divider #(.width(32)) divider_7 (
    .a(divider_5_out), .b(32'ha), .out(divider_7_out),
    .rem({divider_7_rem_7, divider_7_rem_6, divider_7_rem_5, divider_7_rem_4, divider_7_rem_3, divider_7_rem_2, divider_7_rem, D3}));  // open: upper
  Divider #(.width(32)) divider_8 (
    .a(divider_6_out), .b(32'ha), .out(divider_8_out),
    .rem({divider_8_rem_7, divider_8_rem_6, divider_8_rem_5, divider_8_rem_4, divider_8_rem_3, divider_8_rem_2, divider_8_rem, D8}));  // open: upper
  Divider #(.width(32)) divider_9 (
    .a(divider_7_out), .b(32'ha), .out(divider_9_out),
    .rem({divider_9_rem_7, divider_9_rem_6, divider_9_rem_5, divider_9_rem_4, divider_9_rem_3, divider_9_rem_2, divider_9_rem, D4}));  // open: upper
  Divider #(.width(32)) divider_10 (
    .a(divider_8_out), .b(32'ha),
    .rem({divider_10_rem_7, divider_10_rem_6, divider_10_rem_5, divider_10_rem_4, divider_10_rem_3, divider_10_rem_2, divider_10_rem, D9}));  // open: out, upper
endmodule

module \斐波那契_Fibonacci_数列计算器  (
  input  [5:0] n,
  input  clear,
  input  clock,
  output [3:0] D9,
  output [3:0] D8,
  output [3:0] D7,
  output [3:0] D6,
  output [3:0] D5,
  output [3:0] D4,
  output [3:0] D3,
  output [3:0] D2,
  output [3:0] D1,
  output [3:0] D0
);

  wire \控制器模块_1_clk , \控制器模块_1_clr , \控制器模块_1_ni_1 , \控制器模块_1_start ;
  wire [31:0] \矩阵快速幂算法迭代模块_1_fi ;

  \控制器模块  \u_控制器模块_1  (
    .n(n), .clear(clear), .clock(clock), .clr(\控制器模块_1_clr ), .ni_1(\控制器模块_1_ni_1 ), .clk(\控制器模块_1_clk ),
    .start(\控制器模块_1_start ));
  \矩阵快速幂算法迭代模块  \u_矩阵快速幂算法迭代模块_1  (
    .start(\控制器模块_1_start ), .clr(\控制器模块_1_clr ), .clk(\控制器模块_1_clk ), .ni_1(\控制器模块_1_ni_1 ),
    .Fi(\矩阵快速幂算法迭代模块_1_fi ));
  \Fibonacci数显示模块  \fibonacci数显示模块_1  (
    .Fi(\矩阵快速幂算法迭代模块_1_fi ), .D0(D0), .D1(D1), .D2(D2), .D3(D3), .D4(D4), .D5(D5), .D6(D6), .D7(D7), .D8(D8),
    .D9(D9));
endmodule

module \斐波那契_Fibonacci_数列计算器验证电路  (
  input  [5:0] n
);

  wire clear_out, clock_out;
  wire [3:0] \斐波那契_fibonacci_数列计算器_1_d0 , \斐波那契_fibonacci_数列计算器_1_d1 , \斐波那契_fibonacci_数列计算器_1_d2 ,
       \斐波那契_fibonacci_数列计算器_1_d3 , \斐波那契_fibonacci_数列计算器_1_d4 , \斐波那契_fibonacci_数列计算器_1_d5 ,
       \斐波那契_fibonacci_数列计算器_1_d6 , \斐波那契_fibonacci_数列计算器_1_d7 , \斐波那契_fibonacci_数列计算器_1_d8 ,
       \斐波那契_fibonacci_数列计算器_1_d9 ;

  Button clear (.out(clear_out));
  Button clock (.out(clock_out));
  \斐波那契_Fibonacci_数列计算器  \u_斐波那契_fibonacci_数列计算器_1  (
    .n(n), .clear(clear_out), .clock(clock_out), .D9(\斐波那契_fibonacci_数列计算器_1_d9 ),
    .D8(\斐波那契_fibonacci_数列计算器_1_d8 ), .D7(\斐波那契_fibonacci_数列计算器_1_d7 ), .D6(\斐波那契_fibonacci_数列计算器_1_d6 ),
    .D5(\斐波那契_fibonacci_数列计算器_1_d5 ), .D4(\斐波那契_fibonacci_数列计算器_1_d4 ), .D3(\斐波那契_fibonacci_数列计算器_1_d3 ),
    .D2(\斐波那契_fibonacci_数列计算器_1_d2 ), .D1(\斐波那契_fibonacci_数列计算器_1_d1 ), .D0(\斐波那契_fibonacci_数列计算器_1_d0 ));
  Hex_Digit_Display hex_digit_display_1 (.value(\斐波那契_fibonacci_数列计算器_1_d9 ));  // open: dp
  Hex_Digit_Display hex_digit_display_2 (.value(\斐波那契_fibonacci_数列计算器_1_d8 ));  // open: dp
  Hex_Digit_Display hex_digit_display_3 (.value(\斐波那契_fibonacci_数列计算器_1_d7 ));  // open: dp
  Hex_Digit_Display hex_digit_display_4 (.value(\斐波那契_fibonacci_数列计算器_1_d6 ));  // open: dp
  Hex_Digit_Display hex_digit_display_5 (.value(\斐波那契_fibonacci_数列计算器_1_d5 ));  // open: dp
  Hex_Digit_Display hex_digit_display_6 (.value(\斐波那契_fibonacci_数列计算器_1_d4 ));  // open: dp
  Hex_Digit_Display hex_digit_display_7 (.value(\斐波那契_fibonacci_数列计算器_1_d3 ));  // open: dp
  Hex_Digit_Display hex_digit_display_8 (.value(\斐波那契_fibonacci_数列计算器_1_d2 ));  // open: dp
  Hex_Digit_Display hex_digit_display_9 (.value(\斐波那契_fibonacci_数列计算器_1_d1 ));  // open: dp
  Hex_Digit_Display hex_digit_display_10 (.value(\斐波那契_fibonacci_数列计算器_1_d0 ));  // open: dp
endmodule

module \矩阵快速幂算法迭代模块  (
  input  start,
  input  clr,
  input  clk,
  input  ni_1,
  output [31:0] Fi
);

  wire and_1_out, not_1_out;
  wire [31:0] multiplexer_1_out, multiplexer_2_out, multiplexer_3_out, multiplexer_4_out, multiplexer_5_out,
       multiplexer_6_out, multiplexer_7_out, multiplexer_8_out, register_1_q, register_3_q, register_4_q,
       sqrx_1_a_prime, sqrx_1_b_prime, sqrx_1_c_prime, sqrx_1_d_prime, sqrx_a_1_a_prime_prime,
       sqrx_a_1_b_prime_prime, sqrx_a_1_c_prime_prime, sqrx_a_1_d_prime_prime;

  and and_1 (and_1_out, start, not_1_out);
  not not_1 (not_1_out, clr);
  Multiplexer #(.select(1), .width(32), .disabled("Z"), .enable("false")) multiplexer_1 (
    .in0({32{1'b0}}), .in1(multiplexer_5_out), .out(multiplexer_1_out), .sel(and_1_out));
  Multiplexer #(.select(1), .width(32), .disabled("Z"), .enable("false")) multiplexer_2 (
    .in0(32'h1), .in1(multiplexer_6_out), .out(multiplexer_2_out), .sel(and_1_out));
  Multiplexer #(.select(1), .width(32), .disabled("Z"), .enable("false")) multiplexer_3 (
    .in0(32'h1), .in1(multiplexer_7_out), .out(multiplexer_3_out), .sel(and_1_out));
  Multiplexer #(.select(1), .width(32), .disabled("Z"), .enable("false")) multiplexer_4 (
    .in0(32'h1), .in1(multiplexer_8_out), .out(multiplexer_4_out), .sel(and_1_out));
  Register #(.width(32), .trigger("rising"), .Select("low")) register_1 (
    .D(multiplexer_1_out), .en(1'b1), .Q(register_1_q), .clk(clk), .clr(clr), .preset(1'b0));  // open: cs
  Register #(.width(32), .trigger("rising"), .Select("low")) register_2 (
    .D(multiplexer_2_out), .en(1'b1), .Q(Fi), .clk(clk), .clr(clr), .preset(1'b0));  // open: cs
  Register #(.width(32), .trigger("rising"), .Select("low")) register_3 (
    .D(multiplexer_3_out), .en(1'b1), .Q(register_3_q), .clk(clk), .clr(clr), .preset(1'b0));  // open: cs
  Register #(.width(32), .trigger("rising"), .Select("low")) register_4 (
    .D(multiplexer_4_out), .en(1'b1), .Q(register_4_q), .clk(clk), .clr(clr), .preset(1'b0));  // open: cs
  sqrX sqrx_1 (
    .a(register_1_q), .b(Fi), .c(register_3_q), .d(register_4_q), .a_prime(sqrx_1_a_prime),
    .b_prime(sqrx_1_b_prime), .c_prime(sqrx_1_c_prime), .d_prime(sqrx_1_d_prime));
  sqrX_A sqrx_a_1 (
    .a(register_1_q), .b(Fi), .c(register_3_q), .d(register_4_q), .a_prime_prime(sqrx_a_1_a_prime_prime),
    .b_prime_prime(sqrx_a_1_b_prime_prime), .c_prime_prime(sqrx_a_1_c_prime_prime),
    .d_prime_prime(sqrx_a_1_d_prime_prime));
  Multiplexer #(.select(1), .width(32), .disabled("Z"), .enable("false")) multiplexer_5 (
    .in0(sqrx_1_a_prime), .in1(sqrx_a_1_a_prime_prime), .out(multiplexer_5_out), .sel(ni_1));
  Multiplexer #(.select(1), .width(32), .disabled("Z"), .enable("false")) multiplexer_6 (
    .in0(sqrx_1_b_prime), .in1(sqrx_a_1_b_prime_prime), .out(multiplexer_6_out), .sel(ni_1));
  Multiplexer #(.select(1), .width(32), .disabled("Z"), .enable("false")) multiplexer_7 (
    .in0(sqrx_1_c_prime), .in1(sqrx_a_1_c_prime_prime), .out(multiplexer_7_out), .sel(ni_1));
  Multiplexer #(.select(1), .width(32), .disabled("Z"), .enable("false")) multiplexer_8 (
    .in0(sqrx_1_d_prime), .in1(sqrx_a_1_d_prime_prime), .out(multiplexer_8_out), .sel(ni_1));
endmodule

module \控制器模块  (
  input  [5:0] n,
  input  clear,
  input  clock,
  output clr,
  output ni_1,
  output clk,
  output start
);

  wire comparator_1_lt, not_1_out, or_1_out, or_2_out;
  wire [7:0] counter_1_q;

  not not_1 (not_1_out, clear);
  or or_1 (or_1_out, clear, clock);
  Counter #(.width(8), .max('hff), .ongoal("wrap"), .trigger("rising"), .behavior("new")) counter_1 (
    .Q(counter_1_q), .clk(clock), .clr(clear));  // open: load, D, count, carry, preset, down
  Shift_Register #(.width(1), .length(6), .parallel("true"), .trigger("rising")) shift_register_1 (
    .shift(not_1_out), .in(1'b0), .clk(or_1_out), .out(ni_1), .load(clear), .d0(n[0]), .d1(n[1]), .d2(n[2]),
    .d3(n[3]), .d4(n[4]), .d5(n[5]));  // open: clr, q0, q1, q2, q3, q4, q5
  Comparator #(.width(8), .mode("twosComplement")) comparator_1 (
    .a(counter_1_q), .b(8'h6), .lt(comparator_1_lt));  // open: gt, eq
  and and_1 (clk, comparator_1_lt, clock);
  or or_2 (or_2_out, ni_1, start);
  D_Flip_Flop #(.trigger("rising"), .Pre_Clr_Positions("ABOVE_BELOW"), .NegatePresetClear("false"), .enable("false"), .NewFFLayout("true")) d_ff_1 (
    .clk(clock), .D(or_2_out), .Q(start), .reset(clear));  // open: Qn, preset

  assign clr = clear;
endmodule
